// Digital circuit ALU.dig as structural Verilog
module ALU (
  input  [15:0] x,
  input  [15:0] y,
  input  zx,
  input  no,
  input  nx,
  input  f,
  input  zy,
  input  ny,
  output [15:0] out,
  output zr,
  output ng,
  output of
);

  wire add16_1_carry, or8way_1_out, or8way_2_out, or_1_out;
  wire [15:0] add16_1_out, and16_1_out, mux16_1_out, mux16_2_out, mux16_3_out, mux16_4_out, mux16_5_out,
       not16_1_out, not16_2_out, not16_3_out;

  Mux16 mux16_1 (.a(x), .b({16{1'b0}}), .out(mux16_1_out), .sel(zx));
  Mux16 mux16_2 (.a(y), .b({16{1'b0}}), .out(mux16_2_out), .sel(zy));
  Not16 not16_1 (.in(mux16_1_out), .out(not16_1_out));
  Not16 not16_2 (.in(mux16_2_out), .out(not16_2_out));
  Mux16 mux16_3 (.a(mux16_1_out), .b(not16_1_out), .out(mux16_3_out), .sel(nx));
  Mux16 mux16_4 (.a(mux16_2_out), .b(not16_2_out), .out(mux16_4_out), .sel(ny));
  And16 and16_1 (.a(mux16_3_out), .b(mux16_4_out), .out(and16_1_out));
  Add16 add16_1 (.a(mux16_3_out), .b(mux16_4_out), .out(add16_1_out), .carry(add16_1_carry));
  Mux16 mux16_5 (.a(and16_1_out), .b(add16_1_out), .out(mux16_5_out), .sel(f));
  Not not_1 (.in(or_1_out), .out(zr));
  And and_1 (.a(f), .out(of), .b(add16_1_carry));
  Not16 not16_3 (.in(mux16_5_out), .out(not16_3_out));
  Or or_1 (.a(or8way_2_out), .b(or8way_1_out), .out(or_1_out));
  Mux16 mux16_6 (.a(mux16_5_out), .b(not16_3_out), .out({ng, out[14:0]}), .sel(no));
  Or8Way or8way_1 (.out(or8way_1_out), .in({ng, out[14:8]}));
  Or8Way or8way_2 (.out(or8way_2_out), .in(out[7:0]));

  assign out[15] = ng;
endmodule

/* Test case:
        x                 y         zx nx zy ny  f no        out        
 0b0000000000000000  0b1111111111111111  1  0  1  0  1  0  0b0000000000000000 
 0b0000000000000000  0b1111111111111111  1  1  1  1  1  1  0b0000000000000001 
 0b0000000000000000  0b1111111111111111  1  1  1  0  1  0  0b1111111111111111 
 0b0000000000000000  0b1111111111111111  0  0  1  1  0  0  0b0000000000000000 
 0b0000000000000000  0b1111111111111111  1  1  0  0  0  0  0b1111111111111111 
 0b0000000000000000  0b1111111111111111  0  0  1  1  0  1  0b1111111111111111 
 0b0000000000000000  0b1111111111111111  1  1  0  0  0  1  0b0000000000000000 
 0b0000000000000000  0b1111111111111111  0  0  1  1  1  1  0b0000000000000000 
 0b0000000000000000  0b1111111111111111  1  1  0  0  1  1  0b0000000000000001 
 0b0000000000000000  0b1111111111111111  0  1  1  1  1  1  0b0000000000000001 
 0b0000000000000000  0b1111111111111111  1  1  0  1  1  1  0b0000000000000000 
 0b0000000000000000  0b1111111111111111  0  0  1  1  1  0  0b1111111111111111 
 0b0000000000000000  0b1111111111111111  1  1  0  0  1  0  0b1111111111111110 
 0b0000000000000000  0b1111111111111111  0  0  0  0  1  0  0b1111111111111111 
 0b0000000000000000  0b1111111111111111  0  1  0  0  1  1  0b0000000000000001 
 0b0000000000000000  0b1111111111111111  0  0  0  1  1  1  0b1111111111111111 
 0b0000000000000000  0b1111111111111111  0  0  0  0  0  0  0b0000000000000000 
 0b0000000000000000  0b1111111111111111  0  1  0  1  0  1  0b1111111111111111 
 0b0101101110100000  0b0001111011010010  1  0  1  0  1  0  0b0000000000000000 
 0b0101101110100000  0b0001111011010010  1  1  1  1  1  1  0b0000000000000001 
 0b0101101110100000  0b0001111011010010  1  1  1  0  1  0  0b1111111111111111 
 0b0101101110100000  0b0001111011010010  0  0  1  1  0  0  0b0101101110100000 
 0b0101101110100000  0b0001111011010010  1  1  0  0  0  0  0b0001111011010010 
 0b0101101110100000  0b0001111011010010  0  0  1  1  0  1  0b1010010001011111 
 0b0101101110100000  0b0001111011010010  1  1  0  0  0  1  0b1110000100101101 
 0b0101101110100000  0b0001111011010010  0  0  1  1  1  1  0b1010010001100000 
 0b0101101110100000  0b0001111011010010  1  1  0  0  1  1  0b1110000100101110 
 0b0101101110100000  0b0001111011010010  0  1  1  1  1  1  0b0101101110100001 
 0b0101101110100000  0b0001111011010010  1  1  0  1  1  1  0b0001111011010011 
 0b0101101110100000  0b0001111011010010  0  0  1  1  1  0  0b0101101110011111 
 0b0101101110100000  0b0001111011010010  1  1  0  0  1  0  0b0001111011010001 
 0b0101101110100000  0b0001111011010010  0  0  0  0  1  0  0b0111101001110010 
 0b0101101110100000  0b0001111011010010  0  1  0  0  1  1  0b0011110011001110 
 0b0101101110100000  0b0001111011010010  0  0  0  1  1  1  0b1100001100110010 
 0b0101101110100000  0b0001111011010010  0  0  0  0  0  0  0b0001101010000000 
 0b0101101110100000  0b0001111011010010  0  1  0  1  0  1  0b0101111111110010 
*/

/* Test case:
        x                 y         zx nx zy ny  f no        out        zr ng 
 0b0000000000000000  0b1111111111111111  1  0  1  0  1  0  0b0000000000000000  1  0 
 0b0000000000000000  0b1111111111111111  1  1  1  1  1  1  0b0000000000000001  0  0 
 0b0000000000000000  0b1111111111111111  1  1  1  0  1  0  0b1111111111111111  0  1 
 0b0000000000000000  0b1111111111111111  0  0  1  1  0  0  0b0000000000000000  1  0 
 0b0000000000000000  0b1111111111111111  1  1  0  0  0  0  0b1111111111111111  0  1 
 0b0000000000000000  0b1111111111111111  0  0  1  1  0  1  0b1111111111111111  0  1 
 0b0000000000000000  0b1111111111111111  1  1  0  0  0  1  0b0000000000000000  1  0 
 0b0000000000000000  0b1111111111111111  0  0  1  1  1  1  0b0000000000000000  1  0 
 0b0000000000000000  0b1111111111111111  1  1  0  0  1  1  0b0000000000000001  0  0 
 0b0000000000000000  0b1111111111111111  0  1  1  1  1  1  0b0000000000000001  0  0 
 0b0000000000000000  0b1111111111111111  1  1  0  1  1  1  0b0000000000000000  1  0 
 0b0000000000000000  0b1111111111111111  0  0  1  1  1  0  0b1111111111111111  0  1 
 0b0000000000000000  0b1111111111111111  1  1  0  0  1  0  0b1111111111111110  0  1 
 0b0000000000000000  0b1111111111111111  0  0  0  0  1  0  0b1111111111111111  0  1 
 0b0000000000000000  0b1111111111111111  0  1  0  0  1  1  0b0000000000000001  0  0 
 0b0000000000000000  0b1111111111111111  0  0  0  1  1  1  0b1111111111111111  0  1 
 0b0000000000000000  0b1111111111111111  0  0  0  0  0  0  0b0000000000000000  1  0 
 0b0000000000000000  0b1111111111111111  0  1  0  1  0  1  0b1111111111111111  0  1 
 0b0000000000010001  0b0000000000000011  1  0  1  0  1  0  0b0000000000000000  1  0 
 0b0000000000010001  0b0000000000000011  1  1  1  1  1  1  0b0000000000000001  0  0 
 0b0000000000010001  0b0000000000000011  1  1  1  0  1  0  0b1111111111111111  0  1 
 0b0000000000010001  0b0000000000000011  0  0  1  1  0  0  0b0000000000010001  0  0 
 0b0000000000010001  0b0000000000000011  1  1  0  0  0  0  0b0000000000000011  0  0 
 0b0000000000010001  0b0000000000000011  0  0  1  1  0  1  0b1111111111101110  0  1 
 0b0000000000010001  0b0000000000000011  1  1  0  0  0  1  0b1111111111111100  0  1 
 0b0000000000010001  0b0000000000000011  0  0  1  1  1  1  0b1111111111101111  0  1 
 0b0000000000010001  0b0000000000000011  1  1  0  0  1  1  0b1111111111111101  0  1 
 0b0000000000010001  0b0000000000000011  0  1  1  1  1  1  0b0000000000010010  0  0 
 0b0000000000010001  0b0000000000000011  1  1  0  1  1  1  0b0000000000000100  0  0 
 0b0000000000010001  0b0000000000000011  0  0  1  1  1  0  0b0000000000010000  0  0 
 0b0000000000010001  0b0000000000000011  1  1  0  0  1  0  0b0000000000000010  0  0 
 0b0000000000010001  0b0000000000000011  0  0  0  0  1  0  0b0000000000010100  0  0 
 0b0000000000010001  0b0000000000000011  0  1  0  0  1  1  0b0000000000001110  0  0 
 0b0000000000010001  0b0000000000000011  0  0  0  1  1  1  0b1111111111110010  0  1 
 0b0000000000010001  0b0000000000000011  0  0  0  0  0  0  0b0000000000000001  0  0 
 0b0000000000010001  0b0000000000000011  0  1  0  1  0  1  0b0000000000010011  0  0 
*/
