// Digital circuit Inc16.dig as structural Verilog
module Inc16 (
  input  [15:0] in,
  output [15:0] out,
  output carry
);

  Add16 add16_1 (.a(in), .b(16'h1), .out(out), .carry(carry));
endmodule

/* Test case:
        in               out        
 0b0000000000000000  0b0000000000000001 
 0b1111111111111111  0b0000000000000000 
 0b0000000000000101  0b0000000000000110 
 0b1111111111111011  0b1111111111111100 
*/
