// Digital circuit And.dig as structural Verilog
module And (
  input  a,
  input  b,
  output out
);

  wire nand_1_out;

  nand nand_1 (nand_1_out, a, b);
  Not not_1 (.in(nand_1_out), .out(out));
endmodule

/* Test case:
   a      b     out  
   0      0      0   
   0      1      0   
   1      0      0   
   1      1      1   
*/
