// Digital circuit And16.dig as structural Verilog
module And16 (
  input  [15:0] a,
  input  [15:0] b,
  output [15:0] out
);

  And and_1 (.a(a[0]), .out(out[0]), .b(b[0]));
  And and_2 (.a(a[1]), .out(out[1]), .b(b[1]));
  And and_3 (.a(a[2]), .out(out[2]), .b(b[2]));
  And and_4 (.a(a[3]), .out(out[3]), .b(b[3]));
  And and_5 (.a(a[4]), .out(out[4]), .b(b[4]));
  And and_6 (.a(a[5]), .out(out[5]), .b(b[5]));
  And and_7 (.a(a[6]), .out(out[6]), .b(b[6]));
  And and_8 (.a(a[7]), .out(out[7]), .b(b[7]));
  And and_9 (.a(a[8]), .out(out[8]), .b(b[8]));
  And and_10 (.a(a[9]), .out(out[9]), .b(b[9]));
  And and_11 (.a(a[10]), .out(out[10]), .b(b[10]));
  And and_12 (.a(a[11]), .out(out[11]), .b(b[11]));
  And and_13 (.a(a[12]), .out(out[12]), .b(b[12]));
  And and_14 (.a(a[13]), .out(out[13]), .b(b[13]));
  And and_15 (.a(a[14]), .out(out[14]), .b(b[14]));
  And and_16 (.a(a[15]), .out(out[15]), .b(b[15]));
endmodule

/* Test case:
        a                 b                out        
 0b0000000000000000  0b0000000000000000  0b0000000000000000 
 0b0000000000000000  0b1111111111111111  0b0000000000000000 
 0b1111111111111111  0b1111111111111111  0b1111111111111111 
 0b1010101010101010  0b0101010101010101  0b0000000000000000 
 0b0011110011000011  0b0000111111110000  0b0000110011000000 
 0b0001001000110100  0b1001100001110110  0b0001000000110100 
*/
