// Digital circuit DMux.dig as structural Verilog
module DMux (
  input  in,
  input  sel,
  output a,
  output b
);

  wire not_1_out;

  Not not_1 (.in(sel), .out(not_1_out));
  And and_1 (.a(in), .out(a), .b(not_1_out));
  And and_2 (.a(in), .out(b), .b(sel));
endmodule

/* Test case:
  in     sel     a      b   
   0      0      0      0   
   0      1      0      0   
   1      0      1      0   
   1      1      0      1   
*/
