// Digital circuit DMux4Way.dig as structural Verilog
module DMux4Way (
  input  in,
  input  [1:0] sel,
  output a,
  output b,
  output c,
  output d
);

  wire dmux_1_a, dmux_1_b;

  DMux dmux_1 (.in(in), .a(dmux_1_a), .b(dmux_1_b), .sel(sel[1]));
  DMux dmux_2 (.in(dmux_1_a), .a(a), .b(b), .sel(sel[0]));
  DMux dmux_3 (.in(dmux_1_b), .a(c), .b(d), .sel(sel[0]));
endmodule

/* Test case:
 in   sel    a    b    c    d  
  0    0b00    0    0    0    0  
  0    0b01    0    0    0    0  
  0    0b10    0    0    0    0  
  0    0b11    0    0    0    0  
  1    0b00    1    0    0    0  
  1    0b01    0    1    0    0  
  1    0b10    0    0    1    0  
  1    0b11    0    0    0    1  
*/
