// Digital circuit DMux8Way.dig as structural Verilog
module DMux8Way (
  input  in,
  input  [2:0] sel,
  output a,
  output b,
  output c,
  output d,
  output e,
  output f,
  output g,
  output h
);

  wire dmux_1_a, dmux_1_b;

  DMux dmux_1 (.in(in), .a(dmux_1_a), .b(dmux_1_b), .sel(sel[2]));
  DMux4Way dmux4way_1 (.a(a), .b(b), .c(c), .d(d), .in(dmux_1_a), .sel(sel[1:0]));
  DMux4Way dmux4way_2 (.a(e), .b(f), .c(g), .d(h), .in(dmux_1_b), .sel(sel[1:0]));
endmodule

/* Test case:
 in    sel    a    b    c    d    e    f    g    h  
  0    0b000    0    0    0    0    0    0    0    0  
  0    0b001    0    0    0    0    0    0    0    0  
  0    0b010    0    0    0    0    0    0    0    0  
  0    0b011    0    0    0    0    0    0    0    0  
  0    0b100    0    0    0    0    0    0    0    0  
  0    0b101    0    0    0    0    0    0    0    0  
  0    0b110    0    0    0    0    0    0    0    0  
  0    0b111    0    0    0    0    0    0    0    0  
  1    0b000    1    0    0    0    0    0    0    0  
  1    0b001    0    1    0    0    0    0    0    0  
  1    0b010    0    0    1    0    0    0    0    0  
  1    0b011    0    0    0    1    0    0    0    0  
  1    0b100    0    0    0    0    1    0    0    0  
  1    0b101    0    0    0    0    0    1    0    0  
  1    0b110    0    0    0    0    0    0    1    0  
  1    0b111    0    0    0    0    0    0    0    1  
*/
