// Digital circuit Mux.dig as structural Verilog
module Mux (
  input  a,
  input  b,
  input  sel,
  output out
);

  wire and_1_out, and_2_out, not_1_out;

  Not not_1 (.in(sel), .out(not_1_out));
  And and_1 (.a(b), .out(and_1_out), .b(sel));
  And and_2 (.a(a), .out(and_2_out), .b(not_1_out));
  Or or_1 (.a(and_2_out), .b(and_1_out), .out(out));
endmodule

/* Test case:
   a      b     sel    out  
   0      0      0      0   
   0      0      1      0   
   0      1      0      0   
   0      1      1      1   
   1      0      0      1   
   1      0      1      0   
   1      1      0      1   
   1      1      1      1   
*/
