// Digital circuit Mux16.dig as structural Verilog
module Mux16 (
  input  [15:0] a,
  input  [15:0] b,
  input  sel,
  output [15:0] out
);

  Mux mux_1 (.a(a[0]), .b(b[0]), .sel(sel), .out(out[0]));
  Mux mux_2 (.a(a[8]), .b(b[8]), .sel(sel), .out(out[8]));
  Mux mux_3 (.a(a[1]), .b(b[1]), .sel(sel), .out(out[1]));
  Mux mux_4 (.a(a[9]), .b(b[9]), .sel(sel), .out(out[9]));
  Mux mux_5 (.a(a[2]), .b(b[2]), .sel(sel), .out(out[2]));
  Mux mux_6 (.a(a[10]), .b(b[10]), .sel(sel), .out(out[10]));
  Mux mux_7 (.a(a[3]), .b(b[3]), .sel(sel), .out(out[3]));
  Mux mux_8 (.a(a[11]), .b(b[11]), .sel(sel), .out(out[11]));
  Mux mux_9 (.a(a[4]), .b(b[4]), .sel(sel), .out(out[4]));
  Mux mux_10 (.a(a[12]), .b(b[12]), .sel(sel), .out(out[12]));
  Mux mux_11 (.a(a[5]), .b(b[5]), .sel(sel), .out(out[5]));
  Mux mux_12 (.a(a[13]), .b(b[13]), .sel(sel), .out(out[13]));
  Mux mux_13 (.a(a[6]), .b(b[6]), .sel(sel), .out(out[6]));
  Mux mux_14 (.a(a[14]), .b(b[14]), .sel(sel), .out(out[14]));
  Mux mux_15 (.a(a[7]), .b(b[7]), .sel(sel), .out(out[7]));
  Mux mux_16 (.a(a[15]), .b(b[15]), .sel(sel), .out(out[15]));
endmodule

/* Test case:
        a                 b          sel        out        
 0b0000000000000000  0b0000000000000000   0   0b0000000000000000 
 0b0000000000000000  0b0000000000000000   1   0b0000000000000000 
 0b0000000000000000  0b0001001000110100   0   0b0000000000000000 
 0b0000000000000000  0b0001001000110100   1   0b0001001000110100 
 0b1001100001110110  0b0000000000000000   0   0b1001100001110110 
 0b1001100001110110  0b0000000000000000   1   0b0000000000000000 
 0b1010101010101010  0b0101010101010101   0   0b1010101010101010 
 0b1010101010101010  0b0101010101010101   1   0b0101010101010101 
*/
