// Digital circuit Mux4Way16.dig as structural Verilog
module Mux4Way16 (
  input  [15:0] a,
  input  [15:0] b,
  input  [15:0] c,
  input  [15:0] d,
  input  [1:0] sel,
  output [15:0] out
);

  wire and_1_out;
  wire [15:0] mux16_1_out, mux16_2_out;

  Mux16 mux16_1 (.a(a), .b(b), .out(mux16_1_out), .sel(sel[0]));
  Mux16 mux16_2 (.a(mux16_1_out), .b(c), .out(mux16_2_out), .sel(sel[1]));
  And and_1 (.a(sel[0]), .out(and_1_out), .b(sel[1]));
  Mux16 mux16_3 (.a(mux16_2_out), .b(d), .out(out), .sel(and_1_out));
endmodule

/* Test case:
        a                 b                 c                 d          sel         out        
 0b0000000000000000  0b0000000000000000  0b0000000000000000  0b0000000000000000   0b00   0b0000000000000000 
 0b0000000000000000  0b0000000000000000  0b0000000000000000  0b0000000000000000   0b01   0b0000000000000000 
 0b0000000000000000  0b0000000000000000  0b0000000000000000  0b0000000000000000   0b10   0b0000000000000000 
 0b0000000000000000  0b0000000000000000  0b0000000000000000  0b0000000000000000   0b11   0b0000000000000000 
 0b0001001000110100  0b1001100001110110  0b1010101010101010  0b0101010101010101   0b00   0b0001001000110100 
 0b0001001000110100  0b1001100001110110  0b1010101010101010  0b0101010101010101   0b01   0b1001100001110110 
 0b0001001000110100  0b1001100001110110  0b1010101010101010  0b0101010101010101   0b10   0b1010101010101010 
 0b0001001000110100  0b1001100001110110  0b1010101010101010  0b0101010101010101   0b11   0b0101010101010101 
*/
