// Digital circuit Not16.dig as structural Verilog
module Not16 (
  input  [15:0] in,
  output [15:0] out
);

  Not not_1 (.in(in[0]), .out(out[0]));
  Not not_2 (.in(in[1]), .out(out[1]));
  Not not_3 (.in(in[2]), .out(out[2]));
  Not not_4 (.in(in[3]), .out(out[3]));
  Not not_5 (.in(in[4]), .out(out[4]));
  Not not_6 (.in(in[5]), .out(out[5]));
  Not not_7 (.in(in[6]), .out(out[6]));
  Not not_8 (.in(in[7]), .out(out[7]));
  Not not_9 (.in(in[8]), .out(out[8]));
  Not not_10 (.in(in[9]), .out(out[9]));
  Not not_11 (.in(in[10]), .out(out[10]));
  Not not_12 (.in(in[11]), .out(out[11]));
  Not not_13 (.in(in[12]), .out(out[12]));
  Not not_14 (.in(in[13]), .out(out[13]));
  Not not_15 (.in(in[14]), .out(out[14]));
  Not not_16 (.in(in[15]), .out(out[15]));
endmodule

/* Test case:
        in               out        
 0b0000000000000000  0b1111111111111111 
 0b1111111111111111  0b0000000000000000 
 0b1010101010101010  0b0101010101010101 
 0b0011110011000011  0b1100001100111100 
 0b0001001000110100  0b1110110111001011 
*/
