// Digital circuit Or8Way.dig as structural Verilog
module Or8Way (
  input  [7:0] in,
  output out
);

  wire or_1_out, or_2_out, or_3_out, or_4_out, or_5_out, or_6_out;

  Or or_1 (.a(in[0]), .b(in[1]), .out(or_1_out));
  Or or_2 (.a(or_1_out), .b(in[2]), .out(or_2_out));
  Or or_3 (.a(or_2_out), .b(in[3]), .out(or_3_out));
  Or or_4 (.a(or_3_out), .b(in[4]), .out(or_4_out));
  Or or_5 (.a(or_4_out), .b(in[5]), .out(or_5_out));
  Or or_6 (.a(or_5_out), .b(in[6]), .out(or_6_out));
  Or or_7 (.a(or_6_out), .b(in[7]), .out(out));
endmodule

/* Test case:
     in      out 
  0b00000000    0  
  0b11111111    1  
  0b00010000    1  
  0b00000001    1  
  0b00100110    1  
*/
