// Digital circuit Xor.dig as structural Verilog
module Xor (
  input  a,
  input  b,
  output out
);

  wire nand_1_out, or_1_out;

  nand nand_1 (nand_1_out, a, b);
  Or or_1 (.a(a), .b(b), .out(or_1_out));
  And and_1 (.a(nand_1_out), .out(out), .b(or_1_out));
endmodule

/* Test case:
   a      b     out  
   0      0      0   
   0      1      1   
   1      0      1   
   1      1      0   
*/
