// Digital circuit DFF.dig as structural Verilog
module DFF (
  input  data,
  input  \time ,
  output out
);

  wire dlatch_1_out, not_1_out;

  DLatch dlatch_1 (.data(data), .en(\time ), .out(dlatch_1_out));
  Not not_1 (.in(\time ), .out(not_1_out));
  DLatch dlatch_2 (.data(dlatch_1_out), .en(not_1_out), .out(out));
endmodule

/* Test case Race Condition I guess:
time data out

0 0 x
1 0 x
0 0 0

1 1 0
0 0 0
*/

/* Test case A test that fails because of Race Condition I guess:
time data out

while(out)
  C   0    x
end while

  0   0    0
  0   1    0
  1   0    0
  1   1    0
  0   0    0
  0   1    0
  1   1    0
  0   1    1
  0   0    1
  1   0    1
  1   1    1
  1   0    1
  0   0    0
*/

/* Test case:
time data out

while(out)
  C   0    x
end while

  0   0    0
  0   1    0
  1   0    0
  1   1    0
  0   0    1
  0   1    1
  1   0    1
  1   1    1
  0   0    1
  0   1    1
  1   0    1
  0   0    0
  0   1    0
*/
