// Digital circuit DLatch.dig as structural Verilog
module DLatch (
  input  data,
  input  en,
  output out
);

  wire not_1_out;

  Not not_1 (.in(data), .out(not_1_out));
  SRGatedLatch srgatedlatch_1 (.set(data), .en(en), .reset(not_1_out), .out(out));
endmodule

/* Test case:
en data out

while(out)
1   0    x
end while

0   0    0
0   1    0
1   0    0
1   1    1

0   0    1
1   0    0
0   1    0
1   1    1
1   0    0
*/
