// Digital circuit PC.dig as structural Verilog
module PC (
  input  [15:0] in,
  input  load,
  input  inc,
  input  reset,
  input  \time ,
  output [15:0] out
);

  wire or_1_out, or_2_out;
  wire [15:0] inc16_1_out, mux16_1_out, mux16_2_out;

  Inc16 inc16_1 (.in(out), .out(inc16_1_out));
  Or or_1 (.a(reset), .b(inc), .out(or_1_out));
  Mux16 mux16_1 (.a(inc16_1_out), .b(in), .out(mux16_1_out), .sel(load));
  Or or_2 (.a(load), .b(or_1_out), .out(or_2_out));
  Mux16 mux16_2 (.a(mux16_1_out), .b({16{1'b0}}), .out(mux16_2_out), .sel(reset));
  Register register_1 (.in(mux16_2_out), .load(or_2_out), .\time (\time ), .out(out));
endmodule

/* Test case:
  time     in    reset load   inc    out

   C         (0)   1     0     0         x  
   
   1         (0)   0     0     0        (0) 
   0         (0)   0     0     0        (0) 
   1         (0)   0     0     1        (0) 
   0         (0)   0     0     1        (1) 
   1    (-32123)   0     0     1        (1) 
   0    (-32123)   0     0     1        (2) 
   1    (-32123)   0     1     1        (2) 
   0    (-32123)   0     1     1   (-32123) 
   1    (-32123)   0     0     1   (-32123) 
   0    (-32123)   0     0     1   (-32122) 
   1    (-32123)   0     0     1   (-32122) 
   0    (-32123)   0     0     1   (-32121) 
   1     (12345)   0     1     0   (-32121) 
   0     (12345)   0     1     0    (12345) 
   1     (12345)   1     1     0    (12345) 
   0     (12345)   1     1     0        (0) 
   1     (12345)   0     1     1        (0) 
   0     (12345)   0     1     1    (12345) 
   1     (12345)   1     1     1    (12345) 
   0     (12345)   1     1     1        (0) 
   1     (12345)   0     0     1        (0) 
   0     (12345)   0     0     1        (1) 
   1     (12345)   1     0     1        (1) 
   0     (12345)   1     0     1        (0) 
   1         (0)   0     1     1        (0) 
   0         (0)   0     1     1        (0) 
   1         (0)   0     0     1        (0) 
   0         (0)   0     0     1        (1) 
   1     (22222)   1     0     0        (1) 
   0     (22222)   1     0     0        (0) 
*/
