// Digital circuit RAM16k.dig as structural Verilog
module RAM16k (
  input  [13:0] address,
  input  [15:0] in,
  input  load,
  input  \time ,
  output [15:0] out
);

  wire not_1_out;

  Not not_1 (.in(\time ), .out(not_1_out));
  RAMDualPort #(.AddrBits(14), .Bits(16)) ramdualport_1 (
    .A(address), .Din(in), .str(load), .C(not_1_out), .ld(1'b1), .D(out));
endmodule

/* Test case:
  time     in    load   address    out    
   1         (0)   0        (0)       (0) 
   0         (0)   0        (0)       (0) 
   1         (0)   1        (0)       (0) 
   0         (0)   1        (0)       (0) 
   1      (4321)   0        (0)       (0) 
   0      (4321)   0        (0)       (0) 
   1      (4321)   1     (4321)       (0) 
   0      (4321)   1     (4321)    (4321) 
   1      (4321)   0        (0)       (0) 
   0      (4321)   0        (0)       (0) 
   1     (12345)   0    (12345)       (0) 
   0     (12345)   0    (12345)       (0) 
   1     (12345)   1    (12345)       (0) 
   0     (12345)   1    (12345)   (12345) 
   1     (12345)   0    (12345)   (12345) 
   0     (12345)   0    (12345)   (12345) 
   0     (12345)   0     (4321)    (4321) 
   1     (16383)   0     (4321)    (4321) 
   0     (16383)   0     (4321)    (4321) 
   1     (16383)   1    (16383)       (0) 
   0     (16383)   1    (16383)   (16383) 
   1     (16383)   0    (16383)   (16383) 
   0     (16383)   0    (16383)   (16383) 
   0     (16383)   0    (12345)   (12345) 
   0     (16383)   0    (16383)   (16383) 
   1     (16383)   0    (10920)       (0) 
   0     (16383)   0    (10920)       (0) 
   0     (16383)   0    (10921)       (0) 
   0     (16383)   0    (10922)       (0) 
   0     (16383)   0    (10923)       (0) 
   0     (16383)   0    (10924)       (0) 
   0     (16383)   0    (10925)       (0) 
   0     (16383)   0    (10926)       (0) 
   0     (16383)   0    (10927)       (0) 
   1     (21845)   1    (10920)       (0) 
   0     (21845)   1    (10920)   (21845) 
   1     (21845)   1    (10921)       (0) 
   0     (21845)   1    (10921)   (21845) 
   1     (21845)   1    (10922)       (0) 
   0     (21845)   1    (10922)   (21845) 
   1     (21845)   1    (10923)       (0) 
   0     (21845)   1    (10923)   (21845) 
   1     (21845)   1    (10924)       (0) 
   0     (21845)   1    (10924)   (21845) 
   1     (21845)   1    (10925)       (0) 
   0     (21845)   1    (10925)   (21845) 
   1     (21845)   1    (10926)       (0) 
   0     (21845)   1    (10926)   (21845) 
   1     (21845)   1    (10927)       (0) 
   0     (21845)   1    (10927)   (21845) 
   1     (21845)   0    (10920)   (21845) 
   0     (21845)   0    (10920)   (21845) 
   0     (21845)   0    (10921)   (21845) 
   0     (21845)   0    (10922)   (21845) 
   0     (21845)   0    (10923)   (21845) 
   0     (21845)   0    (10924)   (21845) 
   0     (21845)   0    (10925)   (21845) 
   0     (21845)   0    (10926)   (21845) 
   0     (21845)   0    (10927)   (21845) 
   1    (-21846)   1    (10920)   (21845) 
   0    (-21846)   1    (10920)  (-21846) 
   1    (-21846)   0    (10920)  (-21846) 
   0    (-21846)   0    (10920)  (-21846) 
   0    (-21846)   0    (10921)   (21845) 
   0    (-21846)   0    (10922)   (21845) 
   0    (-21846)   0    (10923)   (21845) 
   0    (-21846)   0    (10924)   (21845) 
   0    (-21846)   0    (10925)   (21845) 
   0    (-21846)   0    (10926)   (21845) 
   0    (-21846)   0    (10927)   (21845) 
   1     (21845)   1    (10920)  (-21846) 
   0     (21845)   1    (10920)   (21845) 
   1    (-21846)   1    (10921)   (21845) 
   0    (-21846)   1    (10921)  (-21846) 
   1    (-21846)   0    (10920)   (21845) 
   0    (-21846)   0    (10920)   (21845) 
   0    (-21846)   0    (10921)  (-21846) 
   0    (-21846)   0    (10922)   (21845) 
   0    (-21846)   0    (10923)   (21845) 
   0    (-21846)   0    (10924)   (21845) 
   0    (-21846)   0    (10925)   (21845) 
   0    (-21846)   0    (10926)   (21845) 
   0    (-21846)   0    (10927)   (21845) 
   1     (21845)   1    (10921)  (-21846) 
   0     (21845)   1    (10921)   (21845) 
   1    (-21846)   1    (10922)   (21845) 
   0    (-21846)   1    (10922)  (-21846) 
   1    (-21846)   0    (10920)   (21845) 
   0    (-21846)   0    (10920)   (21845) 
   0    (-21846)   0    (10921)   (21845) 
   0    (-21846)   0    (10922)  (-21846) 
   0    (-21846)   0    (10923)   (21845) 
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*/
