// Digital circuit RAM4k.dig as structural Verilog
module RAM4k (
  input  [11:0] address,
  input  [15:0] in,
  input  load,
  input  \time ,
  output [15:0] out
);

  wire not_1_out;

  Not not_1 (.in(\time ), .out(not_1_out));
  RAMDualPort #(.AddrBits(12), .Bits(16)) ramdualport_1 (
    .A(address), .Din(in), .str(load), .C(not_1_out), .ld(1'b1), .D(out));
endmodule

/* Test case:
  time     in    load  address   out   
   1         (0)   0       (0)       (0) 
   0         (0)   0       (0)       (0) 
   1         (0)   1       (0)       (0) 
   0         (0)   1       (0)       (0) 
   1      (1111)   0       (0)       (0) 
   0      (1111)   0       (0)       (0) 
   1      (1111)   1    (1111)       (0) 
   0      (1111)   1    (1111)    (1111) 
   1      (1111)   0       (0)       (0) 
   0      (1111)   0       (0)       (0) 
   1      (3513)   0    (3513)       (0) 
   0      (3513)   0    (3513)       (0) 
   1      (3513)   1    (3513)       (0) 
   0      (3513)   1    (3513)    (3513) 
   1      (3513)   0    (3513)    (3513) 
   0      (3513)   0    (3513)    (3513) 
   0      (3513)   0    (1111)    (1111) 
   1      (4095)   0    (1111)    (1111) 
   0      (4095)   0    (1111)    (1111) 
   1      (4095)   1    (4095)       (0) 
   0      (4095)   1    (4095)    (4095) 
   1      (4095)   0    (4095)    (4095) 
   0      (4095)   0    (4095)    (4095) 
   0      (4095)   0    (3513)    (3513) 
   0      (4095)   0    (4095)    (4095) 
   1      (4095)   0    (2728)       (0) 
   0      (4095)   0    (2728)       (0) 
   0      (4095)   0    (2729)       (0) 
   0      (4095)   0    (2730)       (0) 
   0      (4095)   0    (2731)       (0) 
   0      (4095)   0    (2732)       (0) 
   0      (4095)   0    (2733)       (0) 
   0      (4095)   0    (2734)       (0) 
   0      (4095)   0    (2735)       (0) 
   1     (21845)   1    (2728)       (0) 
   0     (21845)   1    (2728)   (21845) 
   1     (21845)   1    (2729)       (0) 
   0     (21845)   1    (2729)   (21845) 
   1     (21845)   1    (2730)       (0) 
   0     (21845)   1    (2730)   (21845) 
   1     (21845)   1    (2731)       (0) 
   0     (21845)   1    (2731)   (21845) 
   1     (21845)   1    (2732)       (0) 
   0     (21845)   1    (2732)   (21845) 
   1     (21845)   1    (2733)       (0) 
   0     (21845)   1    (2733)   (21845) 
   1     (21845)   1    (2734)       (0) 
   0     (21845)   1    (2734)   (21845) 
   1     (21845)   1    (2735)       (0) 
   0     (21845)   1    (2735)   (21845) 
   1     (21845)   0    (2728)   (21845) 
   0     (21845)   0    (2728)   (21845) 
   0     (21845)   0    (2729)   (21845) 
   0     (21845)   0    (2730)   (21845) 
   0     (21845)   0    (2731)   (21845) 
   0     (21845)   0    (2732)   (21845) 
   0     (21845)   0    (2733)   (21845) 
   0     (21845)   0    (2734)   (21845) 
   0     (21845)   0    (2735)   (21845) 
   1    (-21846)   1    (2728)   (21845) 
   0    (-21846)   1    (2728)  (-21846) 
   1    (-21846)   0    (2728)  (-21846) 
   0    (-21846)   0    (2728)  (-21846) 
   0    (-21846)   0    (2729)   (21845) 
   0    (-21846)   0    (2730)   (21845) 
   0    (-21846)   0    (2731)   (21845) 
   0    (-21846)   0    (2732)   (21845) 
   0    (-21846)   0    (2733)   (21845) 
   0    (-21846)   0    (2734)   (21845) 
   0    (-21846)   0    (2735)   (21845) 
   1     (21845)   1    (2728)  (-21846) 
   0     (21845)   1    (2728)   (21845) 
   1    (-21846)   1    (2729)   (21845) 
   0    (-21846)   1    (2729)  (-21846) 
   1    (-21846)   0    (2728)   (21845) 
   0    (-21846)   0    (2728)   (21845) 
   0    (-21846)   0    (2729)  (-21846) 
   0    (-21846)   0    (2730)   (21845) 
   0    (-21846)   0    (2731)   (21845) 
   0    (-21846)   0    (2732)   (21845) 
   0    (-21846)   0    (2733)   (21845) 
   0    (-21846)   0    (2734)   (21845) 
   0    (-21846)   0    (2735)   (21845) 
   1     (21845)   1    (2729)  (-21846) 
   0     (21845)   1    (2729)   (21845) 
   1    (-21846)   1    (2730)   (21845) 
   0    (-21846)   1    (2730)  (-21846) 
   1    (-21846)   0    (2728)   (21845) 
   0    (-21846)   0    (2728)   (21845) 
   0    (-21846)   0    (2729)   (21845) 
   0    (-21846)   0    (2730)  (-21846) 
   0    (-21846)   0    (2731)   (21845) 
   0    (-21846)   0    (2732)   (21845) 
   0    (-21846)   0    (2733)   (21845) 
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*/
