// Digital circuit RAM512.dig as structural Verilog
module RAM512 (
  input  [8:0] address,
  input  [15:0] in,
  input  load,
  input  \time ,
  output [15:0] out
);

  wire l0, l1, l2, l3, l4, l5, l6, l7;
  wire [15:0] o0, o1, o2, o3, o4, o5, o6, o7;

  RAM64 ram64_1 (.address(address[5:0]), .in(in), .load(l0), .out(o0), .\time (\time ));
  RAM64 ram64_2 (.address(address[5:0]), .in(in), .load(l1), .out(o1), .\time (\time ));
  RAM64 ram64_3 (.address(address[5:0]), .in(in), .load(l2), .out(o2), .\time (\time ));
  RAM64 ram64_4 (.address(address[5:0]), .in(in), .load(l3), .out(o3), .\time (\time ));
  DMux8Way dmux8way_1 (.a(l0), .b(l1), .c(l2), .d(l3), .in(load), .sel(address[8:6]), .e(l4), .f(l5), .g(l6), .h(l7));
  RAM64 ram64_5 (.address(address[5:0]), .in(in), .load(l4), .out(o4), .\time (\time ));
  Mux8Way16 mux8way16_1 (.out(out), .a(o0), .b(o1), .c(o2), .d(o3), .sel(address[8:6]), .e(o4), .f(o5), .g(o6), .h(o7));
  RAM64 ram64_6 (.address(address[5:0]), .in(in), .load(l5), .out(o5), .\time (\time ));
  RAM64 ram64_7 (.address(address[5:0]), .in(in), .load(l6), .out(o6), .\time (\time ));
  RAM64 ram64_8 (.address(address[5:0]), .in(in), .load(l7), .out(o7), .\time (\time ));
endmodule

/* Test case:
  time     in    load  address   out   

loop(a, 512)
   C         (0)   1     (a)         x  
end loop
 
   1         (0)   0      (0)       (0) 
   0         (0)   0      (0)       (0) 
   1         (0)   1      (0)       (0) 
   0         (0)   1      (0)       (0) 
   1     (13099)   0      (0)       (0) 
   0     (13099)   0      (0)       (0) 
   1     (13099)   1    (130)       (0) 
   0     (13099)   1    (130)   (13099) 
   1     (13099)   0      (0)       (0) 
   0     (13099)   0      (0)       (0) 
   1      (4729)   0    (472)       (0) 
   0      (4729)   0    (472)       (0) 
   1      (4729)   1    (472)       (0) 
   0      (4729)   1    (472)    (4729) 
   1      (4729)   0    (472)    (4729) 
   0      (4729)   0    (472)    (4729) 
   0      (4729)   0    (130)   (13099) 
   1      (5119)   0    (130)   (13099) 
   0      (5119)   0    (130)   (13099) 
   1      (5119)   1    (511)       (0) 
   0      (5119)   1    (511)    (5119) 
   1      (5119)   0    (511)    (5119) 
   0      (5119)   0    (511)    (5119) 
   0      (5119)   0    (472)    (4729) 
   0      (5119)   0    (511)    (5119) 
   1      (5119)   0    (168)       (0) 
   0      (5119)   0    (168)       (0) 
   0      (5119)   0    (169)       (0) 
   0      (5119)   0    (170)       (0) 
   0      (5119)   0    (171)       (0) 
   0      (5119)   0    (172)       (0) 
   0      (5119)   0    (173)       (0) 
   0      (5119)   0    (174)       (0) 
   0      (5119)   0    (175)       (0) 
   1     (21845)   1    (168)       (0) 
   0     (21845)   1    (168)   (21845) 
   1     (21845)   1    (169)       (0) 
   0     (21845)   1    (169)   (21845) 
   1     (21845)   1    (170)       (0) 
   0     (21845)   1    (170)   (21845) 
   1     (21845)   1    (171)       (0) 
   0     (21845)   1    (171)   (21845) 
   1     (21845)   1    (172)       (0) 
   0     (21845)   1    (172)   (21845) 
   1     (21845)   1    (173)       (0) 
   0     (21845)   1    (173)   (21845) 
   1     (21845)   1    (174)       (0) 
   0     (21845)   1    (174)   (21845) 
   1     (21845)   1    (175)       (0) 
   0     (21845)   1    (175)   (21845) 
   1     (21845)   0    (168)   (21845) 
   0     (21845)   0    (168)   (21845) 
   0     (21845)   0    (169)   (21845) 
   0     (21845)   0    (170)   (21845) 
   0     (21845)   0    (171)   (21845) 
   0     (21845)   0    (172)   (21845) 
   0     (21845)   0    (173)   (21845) 
   0     (21845)   0    (174)   (21845) 
   0     (21845)   0    (175)   (21845) 
   1    (-21846)   1    (168)   (21845) 
   0    (-21846)   1    (168)  (-21846) 
   1    (-21846)   0    (168)  (-21846) 
   0    (-21846)   0    (168)  (-21846) 
   0    (-21846)   0    (169)   (21845) 
   0    (-21846)   0    (170)   (21845) 
   0    (-21846)   0    (171)   (21845) 
   0    (-21846)   0    (172)   (21845) 
   0    (-21846)   0    (173)   (21845) 
   0    (-21846)   0    (174)   (21845) 
   0    (-21846)   0    (175)   (21845) 
   1     (21845)   1    (168)  (-21846) 
   0     (21845)   1    (168)   (21845) 
   1    (-21846)   1    (169)   (21845) 
   0    (-21846)   1    (169)  (-21846) 
   1    (-21846)   0    (168)   (21845) 
   0    (-21846)   0    (168)   (21845) 
   0    (-21846)   0    (169)  (-21846) 
   0    (-21846)   0    (170)   (21845) 
   0    (-21846)   0    (171)   (21845) 
   0    (-21846)   0    (172)   (21845) 
   0    (-21846)   0    (173)   (21845) 
   0    (-21846)   0    (174)   (21845) 
   0    (-21846)   0    (175)   (21845) 
   1     (21845)   1    (169)  (-21846) 
   0     (21845)   1    (169)   (21845) 
   1    (-21846)   1    (170)   (21845) 
   0    (-21846)   1    (170)  (-21846) 
   1    (-21846)   0    (168)   (21845) 
   0    (-21846)   0    (168)   (21845) 
   0    (-21846)   0    (169)   (21845) 
   0    (-21846)   0    (170)  (-21846) 
   0    (-21846)   0    (171)   (21845) 
   0    (-21846)   0    (172)   (21845) 
   0    (-21846)   0    (173)   (21845) 
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*/
