// Digital circuit RAM64.dig as structural Verilog
module RAM64 (
  input  [5:0] address,
  input  [15:0] in,
  input  load,
  input  \time ,
  output [15:0] out
);

  wire l0, l1, l2, l3, l4, l5, l6, l7;
  wire [15:0] o0, o1, o2, o3, o4, o5, o6, o7;

  RAM8 ram8_1 (.address(address[2:0]), .in(in), .load(l0), .out(o0), .\time (\time ));
  RAM8 ram8_2 (.address(address[2:0]), .in(in), .load(l1), .out(o1), .\time (\time ));
  RAM8 ram8_3 (.address(address[2:0]), .in(in), .load(l2), .out(o2), .\time (\time ));
  RAM8 ram8_4 (.address(address[2:0]), .in(in), .load(l3), .out(o3), .\time (\time ));
  DMux8Way dmux8way_1 (.a(l0), .b(l1), .c(l2), .d(l3), .in(load), .sel(address[5:3]), .e(l4), .f(l5), .g(l6), .h(l7));
  RAM8 ram8_5 (.address(address[2:0]), .in(in), .load(l4), .out(o4), .\time (\time ));
  Mux8Way16 mux8way16_1 (.out(out), .a(o0), .b(o1), .c(o2), .d(o3), .sel(address[5:3]), .e(o4), .f(o5), .g(o6), .h(o7));
  RAM8 ram8_6 (.address(address[2:0]), .in(in), .load(l5), .out(o5), .\time (\time ));
  RAM8 ram8_7 (.address(address[2:0]), .in(in), .load(l6), .out(o6), .\time (\time ));
  RAM8 ram8_8 (.address(address[2:0]), .in(in), .load(l7), .out(o7), .\time (\time ));
endmodule

/* Test case:
  time     in    load  address   out   

loop(a, 64)
   C         (0)   1     (a)         x  
end loop
 
   1         (0)   0      (0)       (0) 
   0         (0)   0      (0)       (0) 
   1         (0)   1      (0)       (0) 
   0         (0)   1      (0)       (0) 
   1      (1313)   0      (0)       (0) 
   0      (1313)   0      (0)       (0) 
   1      (1313)   1     (13)       (0) 
   0      (1313)   1     (13)    (1313) 
   1      (1313)   0      (0)       (0) 
   0      (1313)   0      (0)       (0) 
   1      (4747)   0     (47)       (0) 
   0      (4747)   0     (47)       (0) 
   1      (4747)   1     (47)       (0) 
   0      (4747)   1     (47)    (4747) 
   1      (4747)   0     (47)    (4747) 
   0      (4747)   0     (47)    (4747) 
   0      (4747)   0     (13)    (1313) 
   1      (6363)   0     (13)    (1313) 
   0      (6363)   0     (13)    (1313) 
   1      (6363)   1     (63)       (0) 
   0      (6363)   1     (63)    (6363) 
   1      (6363)   0     (63)    (6363) 
   0      (6363)   0     (63)    (6363) 
   0      (6363)   0     (47)    (4747) 
   0      (6363)   0     (63)    (6363) 
   1      (6363)   0     (40)       (0) 
   0      (6363)   0     (40)       (0) 
   0      (6363)   0     (41)       (0) 
   0      (6363)   0     (42)       (0) 
   0      (6363)   0     (43)       (0) 
   0      (6363)   0     (44)       (0) 
   0      (6363)   0     (45)       (0) 
   0      (6363)   0     (46)       (0) 
   0      (6363)   0     (47)    (4747) 
   1     (21845)   1     (40)       (0) 
   0     (21845)   1     (40)   (21845) 
   1     (21845)   1     (41)       (0) 
   0     (21845)   1     (41)   (21845) 
   1     (21845)   1     (42)       (0) 
   0     (21845)   1     (42)   (21845) 
   1     (21845)   1     (43)       (0) 
   0     (21845)   1     (43)   (21845) 
   1     (21845)   1     (44)       (0) 
   0     (21845)   1     (44)   (21845) 
   1     (21845)   1     (45)       (0) 
   0     (21845)   1     (45)   (21845) 
   1     (21845)   1     (46)       (0) 
   0     (21845)   1     (46)   (21845) 
   1     (21845)   1     (47)    (4747) 
   0     (21845)   1     (47)   (21845) 
   1     (21845)   0     (40)   (21845) 
   0     (21845)   0     (40)   (21845) 
   0     (21845)   0     (41)   (21845) 
   0     (21845)   0     (42)   (21845) 
   0     (21845)   0     (43)   (21845) 
   0     (21845)   0     (44)   (21845) 
   0     (21845)   0     (45)   (21845) 
   0     (21845)   0     (46)   (21845) 
   0     (21845)   0     (47)   (21845) 
   1    (-21846)   1     (40)   (21845) 
   0    (-21846)   1     (40)  (-21846) 
   1    (-21846)   0     (40)  (-21846) 
   0    (-21846)   0     (40)  (-21846) 
   0    (-21846)   0     (41)   (21845) 
   0    (-21846)   0     (42)   (21845) 
   0    (-21846)   0     (43)   (21845) 
   0    (-21846)   0     (44)   (21845) 
   0    (-21846)   0     (45)   (21845) 
   0    (-21846)   0     (46)   (21845) 
   0    (-21846)   0     (47)   (21845) 
   1     (21845)   1     (40)  (-21846) 
   0     (21845)   1     (40)   (21845) 
   1    (-21846)   1     (41)   (21845) 
   0    (-21846)   1     (41)  (-21846) 
   1    (-21846)   0     (40)   (21845) 
   0    (-21846)   0     (40)   (21845) 
   0    (-21846)   0     (41)  (-21846) 
   0    (-21846)   0     (42)   (21845) 
   0    (-21846)   0     (43)   (21845) 
   0    (-21846)   0     (44)   (21845) 
   0    (-21846)   0     (45)   (21845) 
   0    (-21846)   0     (46)   (21845) 
   0    (-21846)   0     (47)   (21845) 
   1     (21845)   1     (41)  (-21846) 
   0     (21845)   1     (41)   (21845) 
   1    (-21846)   1     (42)   (21845) 
   0    (-21846)   1     (42)  (-21846) 
   1    (-21846)   0     (40)   (21845) 
   0    (-21846)   0     (40)   (21845) 
   0    (-21846)   0     (41)   (21845) 
   0    (-21846)   0     (42)  (-21846) 
   0    (-21846)   0     (43)   (21845) 
   0    (-21846)   0     (44)   (21845) 
   0    (-21846)   0     (45)   (21845) 
   0    (-21846)   0     (46)   (21845) 
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*/
