// Digital circuit RAM8.dig as structural Verilog
module RAM8 (
  input  [2:0] address,
  input  [15:0] in,
  input  load,
  input  \time ,
  output [15:0] out
);

  wire l0, l1, l2, l3, l4, l5, l6, l7;
  wire [15:0] o0, o1, o2, o3, o4, o5, o6, o7;

  Register register_1 (.in(in), .load(l0), .\time (\time ), .out(o0));
  Register register_2 (.in(in), .load(l1), .\time (\time ), .out(o1));
  Register register_3 (.in(in), .load(l2), .\time (\time ), .out(o2));
  DMux8Way dmux8way_1 (.a(l0), .b(l1), .c(l2), .d(l3), .in(load), .sel(address), .e(l4), .f(l5), .g(l6), .h(l7));
  Register register_4 (.in(in), .load(l3), .\time (\time ), .out(o3));
  Mux8Way16 mux8way16_1 (.out(out), .a(o0), .b(o1), .c(o2), .d(o3), .sel(address), .e(o4), .f(o5), .g(o6), .h(o7));
  Register register_5 (.in(in), .load(l4), .\time (\time ), .out(o4));
  Register register_6 (.in(in), .load(l5), .\time (\time ), .out(o5));
  Register register_7 (.in(in), .load(l6), .\time (\time ), .out(o6));
  Register register_8 (.in(in), .load(l7), .\time (\time ), .out(o7));
endmodule

/* Test case:
  time     in    load  address   out    

loop(a, 8)
   C         (0)   1     (a)         x  
end loop

   1         (0)   0     (0)        (0) 
   0         (0)   0     (0)        (0) 
   1         (0)   1     (0)        (0) 
   0         (0)   1     (0)        (0) 
   1     (11111)   0     (0)        (0) 
   0     (11111)   0     (0)        (0) 
   1     (11111)   1     (1)        (0) 
   0     (11111)   1     (1)    (11111) 
   1     (11111)   0     (0)        (0) 
   0     (11111)   0     (0)        (0) 
   1      (3333)   0     (3)        (0) 
   0      (3333)   0     (3)        (0) 
   1      (3333)   1     (3)        (0) 
   0      (3333)   1     (3)     (3333) 
   1      (3333)   0     (3)     (3333) 
   0      (3333)   0     (3)     (3333) 
   0      (3333)   0     (1)    (11111) 
   1      (7777)   0     (1)    (11111) 
   0      (7777)   0     (1)    (11111) 
   1      (7777)   1     (7)        (0) 
   0      (7777)   1     (7)     (7777) 
   1      (7777)   0     (7)     (7777) 
   0      (7777)   0     (7)     (7777) 
   0      (7777)   0     (3)     (3333) 
   0      (7777)   0     (7)     (7777) 
   1      (7777)   0     (0)        (0) 
   0      (7777)   0     (0)        (0) 
   0      (7777)   0     (1)    (11111) 
   0      (7777)   0     (2)        (0) 
   0      (7777)   0     (3)     (3333) 
   0      (7777)   0     (4)        (0) 
   0      (7777)   0     (5)        (0) 
   0      (7777)   0     (6)        (0) 
   0      (7777)   0     (7)     (7777) 
   1     (21845)   1     (0)        (0) 
   0     (21845)   1     (0)    (21845) 
   1     (21845)   1     (1)    (11111) 
   0     (21845)   1     (1)    (21845) 
   1     (21845)   1     (2)        (0) 
   0     (21845)   1     (2)    (21845) 
   1     (21845)   1     (3)     (3333) 
   0     (21845)   1     (3)    (21845) 
   1     (21845)   1     (4)        (0) 
   0     (21845)   1     (4)    (21845) 
   1     (21845)   1     (5)        (0) 
   0     (21845)   1     (5)    (21845) 
   1     (21845)   1     (6)        (0) 
   0     (21845)   1     (6)    (21845) 
   1     (21845)   1     (7)     (7777) 
   0     (21845)   1     (7)    (21845) 
   1     (21845)   0     (0)    (21845) 
   0     (21845)   0     (0)    (21845) 
   0     (21845)   0     (1)    (21845) 
   0     (21845)   0     (2)    (21845) 
   0     (21845)   0     (3)    (21845) 
   0     (21845)   0     (4)    (21845) 
   0     (21845)   0     (5)    (21845) 
   0     (21845)   0     (6)    (21845) 
   0     (21845)   0     (7)    (21845) 
   1    (-21846)   1     (0)    (21845) 
   0    (-21846)   1     (0)   (-21846) 
   1    (-21846)   0     (0)   (-21846) 
   0    (-21846)   0     (0)   (-21846) 
   0    (-21846)   0     (1)    (21845) 
   0    (-21846)   0     (2)    (21845) 
   0    (-21846)   0     (3)    (21845) 
   0    (-21846)   0     (4)    (21845) 
   0    (-21846)   0     (5)    (21845) 
   0    (-21846)   0     (6)    (21845) 
   0    (-21846)   0     (7)    (21845) 
   1     (21845)   1     (0)   (-21846) 
   0     (21845)   1     (0)    (21845) 
   1    (-21846)   1     (1)    (21845) 
   0    (-21846)   1     (1)   (-21846) 
   1    (-21846)   0     (0)    (21845) 
   0    (-21846)   0     (0)    (21845) 
   0    (-21846)   0     (1)   (-21846) 
   0    (-21846)   0     (2)    (21845) 
   0    (-21846)   0     (3)    (21845) 
   0    (-21846)   0     (4)    (21845) 
   0    (-21846)   0     (5)    (21845) 
   0    (-21846)   0     (6)    (21845) 
   0    (-21846)   0     (7)    (21845) 
   1     (21845)   1     (1)   (-21846) 
   0     (21845)   1     (1)    (21845) 
   1    (-21846)   1     (2)    (21845) 
   0    (-21846)   1     (2)   (-21846) 
   1    (-21846)   0     (0)    (21845) 
   0    (-21846)   0     (0)    (21845) 
   0    (-21846)   0     (1)    (21845) 
   0    (-21846)   0     (2)   (-21846) 
   0    (-21846)   0     (3)    (21845) 
   0    (-21846)   0     (4)    (21845) 
   0    (-21846)   0     (5)    (21845) 
   0    (-21846)   0     (6)    (21845) 
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*/
