// Digital circuit Register.dig as structural Verilog
module Register (
  input  [15:0] in,
  input  load,
  input  \time ,
  output [15:0] out
);

  Bit bit_1 (.in(in[0]), .load(load), .\time (\time ), .out(out[0]));
  Bit bit_2 (.in(in[1]), .load(load), .\time (\time ), .out(out[1]));
  Bit bit_3 (.in(in[2]), .load(load), .\time (\time ), .out(out[2]));
  Bit bit_4 (.in(in[3]), .load(load), .\time (\time ), .out(out[3]));
  Bit bit_5 (.in(in[4]), .load(load), .\time (\time ), .out(out[4]));
  Bit bit_6 (.in(in[5]), .load(load), .\time (\time ), .out(out[5]));
  Bit bit_7 (.in(in[6]), .load(load), .\time (\time ), .out(out[6]));
  Bit bit_8 (.in(in[7]), .load(load), .\time (\time ), .out(out[7]));
  Bit bit_9 (.in(in[8]), .load(load), .\time (\time ), .out(out[8]));
  Bit bit_10 (.in(in[9]), .load(load), .\time (\time ), .out(out[9]));
  Bit bit_11 (.in(in[10]), .load(load), .\time (\time ), .out(out[10]));
  Bit bit_12 (.in(in[11]), .load(load), .\time (\time ), .out(out[11]));
  Bit bit_13 (.in(in[12]), .load(load), .\time (\time ), .out(out[12]));
  Bit bit_14 (.in(in[13]), .load(load), .\time (\time ), .out(out[13]));
  Bit bit_15 (.in(in[14]), .load(load), .\time (\time ), .out(out[14]));
  Bit bit_16 (.in(in[15]), .load(load), .\time (\time ), .out(out[15]));
endmodule

/* Test case:
  time     in    load    out    

while(out != (0))
   C         (0)   1        x 
end while

   1         (0)   0        (0) 
   0         (0)   0        (0) 
   1         (0)   1        (0) 
   0         (0)   1        (0) 
   1    (-32123)   0        (0) 
   0    (-32123)   0        (0) 
   1     (11111)   0        (0) 
   0     (11111)   0        (0) 
   1    (-32123)   1        (0) 
   0    (-32123)   1   (-32123) 
   1    (-32123)   1   (-32123) 
   0    (-32123)   1   (-32123) 
   1    (-32123)   0   (-32123) 
   0    (-32123)   0   (-32123) 
   1     (12345)   1   (-32123) 
   0     (12345)   1    (12345) 
   1         (0)   0    (12345) 
   0         (0)   0    (12345) 
   1         (0)   1    (12345) 
   0         (0)   1        (0) 
   1         (1)   0        (0) 
   0         (1)   0        (0) 
   1         (1)   1        (0) 
   0         (1)   1        (1) 
   1         (2)   0        (1) 
   0         (2)   0        (1) 
   1         (2)   1        (1) 
   0         (2)   1        (2) 
   1         (4)   0        (2) 
   0         (4)   0        (2) 
   1         (4)   1        (2) 
   0         (4)   1        (4) 
   1         (8)   0        (4) 
   0         (8)   0        (4) 
   1         (8)   1        (4) 
   0         (8)   1        (8) 
   1        (16)   0        (8) 
   0        (16)   0        (8) 
   1        (16)   1        (8) 
   0        (16)   1       (16) 
   1        (32)   0       (16) 
   0        (32)   0       (16) 
   1        (32)   1       (16) 
   0        (32)   1       (32) 
   1        (64)   0       (32) 
   0        (64)   0       (32) 
   1        (64)   1       (32) 
   0        (64)   1       (64) 
   1       (128)   0       (64) 
   0       (128)   0       (64) 
   1       (128)   1       (64) 
   0       (128)   1      (128) 
   1       (256)   0      (128) 
   0       (256)   0      (128) 
   1       (256)   1      (128) 
   0       (256)   1      (256) 
   1       (512)   0      (256) 
   0       (512)   0      (256) 
   1       (512)   1      (256) 
   0       (512)   1      (512) 
   1      (1024)   0      (512) 
   0      (1024)   0      (512) 
   1      (1024)   1      (512) 
   0      (1024)   1     (1024) 
   1      (2048)   0     (1024) 
   0      (2048)   0     (1024) 
   1      (2048)   1     (1024) 
   0      (2048)   1     (2048) 
   1      (4096)   0     (2048) 
   0      (4096)   0     (2048) 
   1      (4096)   1     (2048) 
   0      (4096)   1     (4096) 
   1      (8192)   0     (4096) 
   0      (8192)   0     (4096) 
   1      (8192)   1     (4096) 
   0      (8192)   1     (8192) 
   1     (16384)   0     (8192) 
   0     (16384)   0     (8192) 
   1     (16384)   1     (8192) 
   0     (16384)   1    (16384) 
   1    (-32768)   0    (16384) 
   0    (-32768)   0    (16384) 
   1    (-32768)   1    (16384) 
   0    (-32768)   1   (-32768) 
   1        (-2)   0   (-32768) 
   0        (-2)   0   (-32768) 
   1        (-2)   1   (-32768) 
   0        (-2)   1       (-2) 
   1        (-3)   0       (-2) 
   0        (-3)   0       (-2) 
   1        (-3)   1       (-2) 
   0        (-3)   1       (-3) 
   1        (-5)   0       (-3) 
   0        (-5)   0       (-3) 
   1        (-5)   1       (-3) 
   0        (-5)   1       (-5) 
   1        (-9)   0       (-5) 
   0        (-9)   0       (-5) 
   1        (-9)   1       (-5) 
   0        (-9)   1       (-9) 
   1       (-17)   0       (-9) 
   0       (-17)   0       (-9) 
   1       (-17)   1       (-9) 
   0       (-17)   1      (-17) 
   1       (-33)   0      (-17) 
   0       (-33)   0      (-17) 
   1       (-33)   1      (-17) 
   0       (-33)   1      (-33) 
   1       (-65)   0      (-33) 
   0       (-65)   0      (-33) 
   1       (-65)   1      (-33) 
   0       (-65)   1      (-65) 
   1      (-129)   0      (-65) 
   0      (-129)   0      (-65) 
   1      (-129)   1      (-65) 
   0      (-129)   1     (-129) 
   1      (-257)   0     (-129) 
   0      (-257)   0     (-129) 
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*/
