// Digital circuit SRGatedLatch.dig as structural Verilog
module SRGatedLatch (
  input  set,
  input  en,
  input  reset,
  output out
);

  wire and_1_out, and_2_out;

  And and_1 (.a(set), .out(and_1_out), .b(en));
  And and_2 (.a(en), .out(and_2_out), .b(reset));
  RS_FF_AS rs_ff_as_1 (.S(and_1_out), .R(and_2_out), .Q(out));  // open: nQ
endmodule

/* Test case:
en set reset out

while(out)
1   0    1    x
end while

0   0    0    0
0   0    1    0
0   1    0    0
0   1    1    0
1   0    0    0
1   0    1    0
1   1    0    1
1   1    1    0

1   1    0    1
0   0    1    1
1   0    1    0
0   1    0    0
*/
