// Digital circuit SRLatch.dig as structural Verilog
module SRLatch (
  input  set,
  input  reset,
  output out
);

  wire not_1_out, or_1_out;

  Or or_1 (.a(out), .b(set), .out(or_1_out));
  Not not_1 (.in(reset), .out(not_1_out));
  And and_1 (.a(or_1_out), .out(out), .b(not_1_out));
endmodule

/* Test case:
set reset out

while(out)
 0    1    x
end while

 0    0    0
 0    1    0
 1    0    1
 1    1    0
*/
